# Fritzing sketch nordic_3 (saved by Fritzing 0.9.2b)

parts:
  Part1 = Arduino Uno (Rev3)
  NRF24L2 = NRF24L01

nets:
  N1: Part1.D8, NRF24L2.IRQ
  N2: Part1.D9_PWM, NRF24L2.CE
  N3: Part1.D10_PWM/SS, NRF24L2.CSN
  N4: Part1.D11_PWM/MOSI, NRF24L2.MOSI
  N5: Part1.D12/MISO, NRF24L2.MISO
  N6: Part1.D13/SCK, NRF24L2.SCK
  GND: Part1.GND, NRF24L2.GND
  3V3: Part1.3V3, NRF24L2.VCC

custom parts:
  NRF24L01: NRF24L01 module
